# Fritzing sketch SADD (saved by Fritzing 0.9.3b)
breadboards: 1

parts:
  Part1 = Arduino Nano (Rev3.0) (ICSP)
  VCC1 = 4 x AAA Battery Mount
  Part2 = TRRS 3.5mm Jack Breakout
  GY1 = MPU-6050 Board GY-521 [form="♀ (female)" package=THT]
  S1 = SWITCH-MOMENTARY-2 [package=tactile-pth]
  R1 = Resistor [tolerance=±5% resistance=220 package="0603 [SMD]"]

nets:
  N1: Part1.GND, VCC1.-, Part2.RING2, GY1.pin2, S1.2
  N2: Part1.D5, S1.1, R1.Pin_1
  N3: Part1.D9, Part2.TIP
  N4: Part1.D10, Part2.RING1
  N5: Part1.VIN, VCC1.+
  N6: Part1.5V, GY1.pin1
  N7: Part1.A5, GY1.pin3
  N8: Part1.A4, GY1.pin4

custom parts:
  MPU-6050 Board GY-521: Acelerometro y Giroscopio MPU-6050 Board GY-521
